# Fritzing sketch esp8266_ssd1306_ (saved by Fritzing 0.9.3b)
circuit board: 5.15981cm x 4.23632cm
breadboards: 1

parts:
  U1 = ESP8266 WiFi Module [part_number=ESP8266]
  R1 = Resistor [tolerance=±5% resistance=1.8k package=THT]
  R2 = Resistor [tolerance=±5% resistance=1.8k package=THT]
  Squix2 = OLED 0.96" 128x64 I2C SSD1306
  C1 = Electrolytic Capacitor [capacitance=1µF package="100 mil [THT, electrolytic]"]
  S1 = Pushbutton [package="[THT]"]  # not connected
  Bauteil1 = FTDI Basic Programmer

nets:
  N1: U1.RXD, Bauteil1.TXO
  VCC: U1.VCC, U1.RST, U1.CH_PD, R1.Pin_0, R2.Pin_0, Squix2.VCC, C1.+, Bauteil1.POWER
  N2: U1.GPIO_0, R1.Pin_1, Squix2.SCL
  GND: U1.GPIO_2, R2.Pin_1, Squix2.GND, Squix2.SCA, C1.-, Bauteil1.GND
  N3: U1.TXD, Bauteil1.RXI

custom parts:
  ESP8266 WiFi Module: Generic WiFi Module based on the ESP8266 with onboard PCB antenna and UART communications
